# Fritzing sketch circuit (saved by Fritzing 0.9.6b)
breadboards: 1

parts:
  J1 = STM32 Nucleo boards
  Componente1 = Arduino Uno (Rev3) - ICSP
  HC-SR04_Sensor_1 = HC-SR04 Ultrasonic Distance Sensor
  J2 = Piezo Speaker
  Componente2 = InvenSense MPU6050
  BN-880 = SUP500F [package=sup500f]  # not connected
  R1 = Resistor [tolerance=±5% power=0.25 resistance=220 package=THT]

nets:
  GND: J1.GND, Componente1.GND
  N1: Componente1.D12/MISO, HC-SR04_Sensor_1.TRIG
  N2: Componente1.D13/SCK, HC-SR04_Sensor_1.ECHO
  GND_2: HC-SR04_Sensor_1.GND, Componente2.GND, R1.Pin_1
  N3: J2.pin1, R1.Pin_0

notes:
  BN-880:
  GND: Black
  VCC: Red
  TX: Green
